# Fritzing sketch extruder control 3 (saved by Fritzing 0.9.3b)
circuit board: 10.1776cm x 5.36194cm
breadboards: 1

parts:
  Part1 = Arduino Mega 2560 (Rev3)
  J2 = Screw terminal - 2 pins [package=THT]
  J13 = screw terminal, 8 pins
  J1 = screw terminal, 7 pins
  J14 = screw terminal, 4 pins
  R29 = Resistor [tolerance=±5% resistance=100 package="0805 [SMD]"]
  R32 = Resistor [tolerance=±5% resistance=100 package="0805 [SMD]"]
  C17 = Ceramic Capacitor [capacitance=0.01µF package="0805 [SMD, multilayer]"]
  C29 = Tantalum Capacitor [capacitance=10µF package="B 3528 [SMD, tantalum]"]
  C20 = Ceramic Capacitor [capacitance=1µF package="0805 [SMD, multilayer]"]
  R35 = Resistor [tolerance=±5% resistance=1M package="0805 [SMD]"]
  C26 = Ceramic Capacitor [capacitance=0.1µF package="0805 [SMD, multilayer]"]
  C23 = Ceramic Capacitor [capacitance=0.01µF package="0805 [SMD, multilayer]"]
  IC5 = SO08 [chip_label=AD8495 package=SO]
  J11 = Screw terminal - 2 pins [package=THT]
  C30 = Ceramic Capacitor [capacitance=0.01µF package="0805 [SMD, multilayer]"]
  C31 = Ceramic Capacitor [capacitance=1µF package="0805 [SMD, multilayer]"]
  C32 = Ceramic Capacitor [capacitance=0.01µF package="0805 [SMD, multilayer]"]
  R36 = Resistor [tolerance=±5% resistance=100 package="0805 [SMD]"]
  R37 = Resistor [tolerance=±5% resistance=100 package="0805 [SMD]"]
  R38 = Resistor [tolerance=±5% resistance=1M package="0805 [SMD]"]
  IC6 = SO08 [chip_label=AD8495 package=SO]
  J15 = Screw terminal - 2 pins [package=THT]
  C33 = Ceramic Capacitor [capacitance=0.1µF package="0805 [SMD, multilayer]"]
  C34 = Tantalum Capacitor [capacitance=10µF package="B 3528 [SMD, tantalum]"]
  C35 = Ceramic Capacitor [capacitance=0.01µF package="0805 [SMD, multilayer]"]
  C36 = Ceramic Capacitor [capacitance=1µF package="0805 [SMD, multilayer]"]
  C37 = Ceramic Capacitor [capacitance=0.01µF package="0805 [SMD, multilayer]"]
  R39 = Resistor [tolerance=±5% resistance=100 package="0805 [SMD]"]
  R40 = Resistor [tolerance=±5% resistance=100 package="0805 [SMD]"]
  R41 = Resistor [tolerance=±5% resistance=1M package="0805 [SMD]"]
  IC7 = SO08 [chip_label=AD8495 package=SO]
  J16 = Screw terminal - 2 pins [package=THT]
  C38 = Ceramic Capacitor [capacitance=0.1µF package="0805 [SMD, multilayer]"]
  C39 = Tantalum Capacitor [capacitance=10µF package="B 3528 [SMD, tantalum]"]
  C40 = Ceramic Capacitor [capacitance=0.01µF package="0805 [SMD, multilayer]"]
  C41 = Ceramic Capacitor [capacitance=1µF package="0805 [SMD, multilayer]"]
  C42 = Ceramic Capacitor [capacitance=0.01µF package="0805 [SMD, multilayer]"]
  R42 = Resistor [tolerance=±5% resistance=100 package="0805 [SMD]"]
  R43 = Resistor [tolerance=±5% resistance=100 package="0805 [SMD]"]
  R44 = Resistor [tolerance=±5% resistance=1M package="0805 [SMD]"]
  J17 = Screw terminal - 2 pins [package=THT]
  C43 = Ceramic Capacitor [capacitance=0.1µF package="0805 [SMD, multilayer]"]
  C44 = Tantalum Capacitor [capacitance=10µF package="B 3528 [SMD, tantalum]"]
  IC8 = SO08 [chip_label=AD8495 package=SO]
  U5 = mystery part, 3 pins [chip_label=LM7805]
  C45 = Tantalum Capacitor [capacitance=47µF package="B 3528 [SMD, tantalum]"]
  C46 = Tantalum Capacitor [capacitance=10µF package="B 3528 [SMD, tantalum]"]
  C47 = Ceramic Capacitor [capacitance=0.1µF package="0805 [SMD, multilayer]"]

nets:
  TC1: Part1.A0, IC6.5, IC6.6
  TC2: Part1.A1, IC5.5, IC5.6
  TC3: Part1.A2, IC7.5, IC7.6
  TC4: Part1.A3, IC8.5, IC8.6
  slc: Part1.D21/SCL, J1.pin4
  sda: Part1.D20/SDA, J1.pin3
  button: Part1.D19/RX1, J1.pin7
  enc 2: Part1.D18/TX1, J1.pin6
  enc 1: Part1.D17_PWM/RX2, J1.pin5
  GND: Part1.GND, J2.pin1, J13.pin2, J13.pin4, J13.pin6, J13.pin8, J1.pin2, C17.1, C23.0, C30.1, C32.0, C35.1, C37.0, C40.1, C42.0, U5.pin2, C45.-, C46.-, C47.0
  5V: Part1.VIN, J2.pin2, J1.pin1, C29.+, C26.1, IC5.7, IC6.7, C33.1, C34.+, IC7.7, C38.1, C39.+, C43.1, C44.+, IC8.7, U5.pin1, C45.+, C46.+
  DI: Part1.D4_PWM, J14.pin4
  DE: Part1.D5_PWM, J14.pin3
  RE: Part1.D6_PWM, J14.pin2
  RO: Part1.D7_PWM, J14.pin1
  ssr1: Part1.D22, J13.pin1
  ssr2: Part1.D24, J13.pin3
  ssr3: Part1.D26, J13.pin5
  ssr4: Part1.D28, J13.pin7
  N1: R29.Pin_0, C17.0, C20.1, IC5.8
  N2: R29.Pin_1, J11.pin1
  N3: R32.Pin_0, C20.0, C23.1, IC5.1
  N4: R32.Pin_1, R35.Pin_1, J11.pin2
  N5: C29.-, R35.Pin_0, C26.0, IC5.2, IC5.3
  N6: C30.0, C31.1, R36.Pin_0, IC6.8
  N7: C31.0, C32.1, R37.Pin_0, IC6.1
  N8: R36.Pin_1, J15.pin1
  N9: R37.Pin_1, R38.Pin_1, J15.pin2
  N10: R38.Pin_0, IC6.2, IC6.3, C33.0, C34.-
  N11: C35.0, C36.1, R39.Pin_0, IC7.8
  N12: C36.0, C37.1, R40.Pin_0, IC7.1
  N13: R39.Pin_1, J16.pin1
  N14: R40.Pin_1, R41.Pin_1, J16.pin2
  N15: R41.Pin_0, IC7.2, IC7.3, C38.0, C39.-
  N16: C40.0, C41.1, R42.Pin_0, IC8.8
  N17: C41.0, C42.1, R43.Pin_0, IC8.1
  N18: R42.Pin_1, J17.pin1
  N19: R43.Pin_1, R44.Pin_1, J17.pin2
  N20: R44.Pin_0, C43.0, C44.-, IC8.2, IC8.3
  N21: U5.pin3, C47.1

notes:
  power in
  control pannel
  Relay Out
  thermocouple 2
  thermocouple 1
  thermocouple 3
  thermocouple 4
  VFD Breakout
